# Fritzing sketch Iteration 1 - v0.1 (saved by Fritzing 0.9.3b)
breadboards: 1

parts:
  Part1 = Adafruit HUZZAH32 ESP32 Feather [part_number="Adafruit #3405"]
  Part2 = Adafruit Ultimate GPS v3 [part_number="Adafruit #746"]
  BATT1 = LiPoly Battery (1300mAh)

nets:
  GND: Part1.GND, Part2.GND
  3.3V: Part1.3.3V, Part2.VIN
  N1: BATT1.positive, BATT1.negative

custom parts:
  Adafruit Ultimate GPS v3: We carry a few different GPS modules here in the Adafruit shop, but none that satisfied our every desire - that's why we designed this little GPS breakout board. We believe this is the Ultimate GPS module, so we named it that. It's got everything you want and more: -165 dBm sensitivity, 10 Hz updates, 66 channels 5V friendly design and only 20mA current draw Breadboard friendly + two mounting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
  LiPoly Battery (1300mAh): Lithium Ion Polymer Battery (1300mAh)
