# Fritzing sketch Iteration 1 - v0.1 (saved by Fritzing 0.9.3b)

parts:
  Part1 = Adafruit HUZZAH32 ESP32 Feather [part_number="Adafruit #3405"]  # not connected
  Part2 = Adafruit Ultimate GPS v3 [part_number="Adafruit #746"]  # not connected
  BATT1 = LiPoly Battery (1300mAh)
  Part3 = Adafruit Adalogger FeatherWing [part_number="Adafruit #2922"]  # not connected

nets:
  N1: BATT1.positive, BATT1.negative

custom parts:
  Adafruit Ultimate GPS v3: We carry a few different GPS modules here in the Adafruit shop, but none that satisfied our every desire - that's why we designed this little GPS breakout board. We believe this is the Ultimate GPS module, so we named it that. It's got everything you want and more: -165 dBm sensitivity, 10 Hz updates, 66 channels 5V friendly design and only 20mA current draw Breadboard friendly + two mounting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
  LiPoly Battery (1300mAh): Lithium Ion Polymer Battery (1300mAh)
  Adafruit Adalogger FeatherWing: This is the Adalogger FeatherWing: it adds both a battery-backed Real Time Clock and micro SD card storage to any Feather main board. This FeatherWing will make it real easy to add datalogging to any of our existing Feathers. You get both an I2C real time clock (PCF8523) with 32KHz crystal and battery backup, and a microSD socket that connects to the SPI port pins (+ extra pin for CS). Tested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
